# Fritzing sketch Diagrama Solar Tracker (saved by Fritzing 1.0.0rc)
circuit board: 16.9333cm x 5.64444cm
breadboards: 1

parts:
  R1 = Resistor [tolerance=±5% resistance=51 power=0.25W package=THT]
  R2 = Resistor [tolerance=±5% resistance=100 power=0.25W package=THT]
  C1 = Electrolytic Capacitor [capacitance=1µF package="100 mil [THT, electrolytic]"]
  LED_PIN_12_(Left) = LED - 5mm [color="Red (633nm)" current=0.030A package="5 mm [THT]"]
  LED_PIN_11_(Right) = LED - 5mm [color="Red (633nm)" current=0.030A package="5 mm [THT]"]
  LED_PIN_13_(Down) = LED - 5mm [color="Red (633nm)" current=0.030A package="5 mm [THT]"]
  LED_PIN_10_(UP) = LED - 5mm [color="Red (633nm)" current=0.030A package="5 mm [THT]"]
  R9 = Resistor [tolerance=±5% resistance=220 power=0.25W package=THT]
  R10 = Resistor [tolerance=±5% resistance=220 power=0.25W package=THT]
  R11 = Resistor [tolerance=±5% resistance=220 power=0.25W package=THT]
  R12 = Resistor [tolerance=±5% resistance=220 power=0.25W package=THT]
  R5 = Resistor [tolerance=±5% resistance=220 power=0.25W package=THT]
  R4 = Resistor [tolerance=±5% resistance=220 power=0.25W package=THT]
  R3 = Resistor [tolerance=±5% resistance=220 power=0.25W package=THT]
  R6 = Resistor [tolerance=±5% resistance=220 power=0.25W package=THT]
  Servo_Vertical = Basic Servo [part_number="HiTec HS-422"]
  Servo_Horizonal = Basic Servo [part_number="HiTec HS-422"]
  SP1 = Solar Pannel
  LDR_2_Right_PIN_A1 = Photocell (LDR) [power=0.25W dark_resistance_@0.01lx=300kΩ light_resistance_@100lx=400Ω luminance=10lx package=THT]
  LDR_4_UP_PIN_A3 = Photocell (LDR) [power=0.25W dark_resistance_@0.01lx=300kΩ light_resistance_@100lx=400Ω luminance=10lx package=THT]
  LDR_3_Down_PIN_A2 = Photocell (LDR) [power=0.25W dark_resistance_@0.01lx=300kΩ light_resistance_@100lx=400Ω luminance=10lx package=THT]
  LDR_1_Left_PIN_A0 = Photocell (LDR) [power=0.25W dark_resistance_@0.01lx=300kΩ light_resistance_@100lx=400Ω luminance=10lx package=THT]
  R8 = Rotary Potentiometer (Small) [maximum_resistance=10kΩ knob_status=50% power=0.5W package=THT]
  Arduino1 = Arduino Uno (Rev3)
  U2 = NodeMCU V3.0  # not connected
  Tiny_RTC1 = Tiny RTC  # not connected
  Componente1 = ACS712 Current Sensor 5A 20A 30A  # not connected
  OLED2 = 128x64 Monochrom OLED Display with SPI Control  # not connected

nets:
  GND: R1.Pin_0, C1.-, LED_PIN_12_(Left).cathode, LED_PIN_11_(Right).cathode, LED_PIN_13_(Down).cathode, LED_PIN_10_(UP).cathode, Servo_Vertical.gnd, Servo_Horizonal.gnd, SP1.pin1, LDR_2_Right_PIN_A1.pin_1, LDR_4_UP_PIN_A3.pin_1, LDR_3_Down_PIN_A2.pin_1, LDR_1_Left_PIN_A0.pin_1, R8.leg1
  N1: R2.Pin_1, SP1.pin2
  N2: LED_PIN_12_(Left).anode, R11.Pin_1
  N3: LED_PIN_11_(Right).anode, LED_PIN_13_(Down).anode, R10.Pin_1, R12.Pin_1
  N4: LED_PIN_10_(UP).anode, R9.Pin_1
  N5: R5.Pin_0, LDR_2_Right_PIN_A1.pin_0, Arduino1.A1
  VCC: R5.Pin_1, R4.Pin_1, R3.Pin_1, R6.Pin_0, Servo_Vertical.vcc, Servo_Horizonal.vcc, R8.leg2
  N6: R4.Pin_0, LDR_3_Down_PIN_A2.pin_0, Arduino1.A2
  N7: R3.Pin_0, LDR_4_UP_PIN_A3.pin_0, Arduino1.A3
  N8: R6.Pin_1, LDR_1_Left_PIN_A0.pin_0, Arduino1.A0

custom parts:
  NodeMCU V3.0: ESP8266 based NodeMCU
  Tiny RTC: Tiny RTC I2C module DS1370Z RTC and AT24C32 EEPROM
  ACS712 Current Sensor 5A 20A 30A: Remix by Michael Kubina http://www.kubina.info Original by: https://forum.fritzing.org/t/current-sensor-5a-acs712/7694 https://forum.fritzing.org/u/ArtHome ArtHome12@gmail.com
