# Fritzing sketch Diagrama Solar Tracker -  nodemcu-v3 Principal - nano Secundario (saved by Fritzing 1.0.0rc)
circuit board: 16.9333cm x 5.64444cm
breadboards: 1

parts:
  LED_ModoManual = LED - 5mm [color="Blue (505nm)" current=0.030A package="5 mm [THT]"]
  LED_SoloMotorHorizontal = LED - 5mm [color="Blue (505nm)" current=0.030A package="5 mm [THT]"]
  LED_ModoAutomatico = LED - 5mm [color="Blue (525nm)" current=0.030A part_number=Led_BTN_Automatico package="5 mm [THT]"]
  R6-LEDModoAutomatico = Resistor [tolerance=±5% resistance=220 power=0.25W package=THT]
  R2-Right_-_10k = Resistor [tolerance=±5% resistance=10k power=0.25W package=THT]
  R3_-_Down_10k = Resistor [tolerance=±5% resistance=10k power=0.25W package=THT]
  R4_-UP_10k = Resistor [tolerance=±5% resistance=10k power=0.25W package=THT]
  R1-_Left_10k = Resistor [tolerance=±5% resistance=10k power=0.25W package=THT]
  LDR_2_Right = Photocell (LDR) [power=0.25W dark_resistance_@0.01lx=300kΩ light_resistance_@100lx=400Ω luminance=10lx package=THT]
  LDR_3_UP_PIN_A3 = Photocell (LDR) [power=0.25W dark_resistance_@0.01lx=300kΩ light_resistance_@100lx=400Ω luminance=10lx package=THT]
  LDR_4_Down_PIN_A2 = Photocell (LDR) [power=0.25W dark_resistance_@0.01lx=300kΩ light_resistance_@100lx=400Ω luminance=10lx package=THT]
  Reloj_Tinyu_RTC = Tiny RTC
  Sensor_Amperaje_ACS712 = ACS712 Current Sensor 5A 20A 30A
  R12-MedirNivelBateria = Resistor [tolerance=±5% resistance=10k power=0.25W package=THT]  # not connected
  Bluetooth = Bluetooth HC-06u [package=THT]  # not connected
  Joystick_KY_023 = Thumb Joystick  # not connected
  BTN_ModoManual = Momentary Switch [package=ksa_sealed_tac_switch]
  Switch-_Encendido = Round Pushbutton  # not connected
  BTN_ModoAutomatico = Momentary Switch [package=ksa_sealed_tac_switch]
  BTN_SoloMotorHorizontal = Momentary Switch [package=ksa_sealed_tac_switch]
  R8-BtnModoManual = Resistor [tolerance=±5% power=0.25W resistance=10 package=THT]
  R9-BtnModoSoloUnMotor = Resistor [tolerance=±5% power=0.25W resistance=10 package=THT]
  R10-ModoAutomatico = Resistor [tolerance=±5% power=0.25W resistance=10 package=THT]
  R6-LEDModoSoloUnMotor = Resistor [tolerance=±5% power=0.25W resistance=220 package=THT]
  R5-LED_ModoManual = Resistor [tolerance=±5% power=0.25W resistance=220 package=THT]
  R18 = Resistor [tolerance=±5% power=0.25W resistance=220 package=THT]  # not connected
  LED_Encendido = LED - 5mm [color="Red (633nm)" current=0.030A package="5 mm [THT]"]  # not connected
  LED_Error = LED - 5mm [color="Red (633nm)" current=0.030A package="5 mm [THT]"]
  Sensor_Voltaje = Voltage Sensor 25V
  LDR_1_Left = Photocell (LDR) [power=0.25W dark_resistance_@0.01lx=300kΩ light_resistance_@100lx=400Ω luminance=10lx package=THT]
  R11-Led_ErrorSD = Resistor [tolerance=±5% power=0.25W resistance=220 package=THT]
  Foto_Celda = Solar Pannel [part_number=FotoSelda]
  Regulado_Voltaje_DC-DC_-12V_5V-5_7A = Mini-360 DC-DC Buck converter [package=THT]
  Servo_Vertical = Basic Servo [part_number="HiTec HS-422"]
  USB_Carga_Externa = USB Connectors [package=usb-a-s-silk-female]  # not connected
  Mod2 = Solar Charge Controller [part_number="KLD Series Solar Charge Controller PWM" package=PWM-Model]
  Micro_controlador_prinsipal_nodemcu-v3-fritzing_V1_3_3V_funciona = NodeMCU V3.0  # not connected
  Servo_Horizonal = Basic Servo [part_number="HiTec HS-422"]
  Componente1 = Arduino Nano (Rev3.0)
  Bat_1 = battery_holder_single_18650
  Bat_2 = battery_holder_single_18650
  Bat_3 = battery_holder_single_18650
  Bat5 = battery_holder_single_18650
  Bat6 = battery_holder_single_18650
  Mod1 = 3S-BMS
  Bat4 = battery_holder_single_18650

nets (from the schematic view):
  N1: LED_ModoManual.cathode, LED_SoloMotorHorizontal.cathode, LED_ModoAutomatico.cathode, Sensor_Amperaje_ACS712.GND
  N2: LED_ModoManual.anode, R5-LED_ModoManual.Pin_1
  N3: LED_SoloMotorHorizontal.anode, R6-LEDModoSoloUnMotor.Pin_1
  N4: LED_ModoAutomatico.anode, R6-LEDModoAutomatico.Pin_1
  N5: R2-Right_-_10k.Pin_0, LDR_2_Right.pin_1, Componente1.A1
  GND: R2-Right_-_10k.Pin_1, R3_-_Down_10k.Pin_0, R4_-UP_10k.Pin_0, R10-ModoAutomatico.Pin_0, Sensor_Voltaje.-, Regulado_Voltaje_DC-DC_-12V_5V-5_7A.OUT-, Servo_Vertical.gnd, Servo_Horizonal.gnd, Componente1.GND
  N6: R3_-_Down_10k.Pin_1, LDR_4_Down_PIN_A2.pin_1, Componente1.A2
  N7: R4_-UP_10k.Pin_1, LDR_3_UP_PIN_A3.pin_1, Componente1.A0
  N8: R1-_Left_10k.Pin_0, LDR_1_Left.pin_1, Componente1.A3
  VCC: LDR_2_Right.pin_0, LDR_3_UP_PIN_A3.pin_0, LDR_4_Down_PIN_A2.pin_0, Sensor_Voltaje.VCC, Sensor_Voltaje.+, LDR_1_Left.pin_0, Servo_Vertical.vcc, Mod2.Connector_3, Servo_Horizonal.vcc, Mod1.+
  N9: Reloj_Tinyu_RTC.GND, LED_Error.cathode
  N10: Sensor_Amperaje_ACS712.2, Sensor_Amperaje_ACS712.OUT
  N11: BTN_ModoManual.4, R8-BtnModoManual.Pin_1
  N12: BTN_ModoAutomatico.4, R10-ModoAutomatico.Pin_1
  N13: BTN_SoloMotorHorizontal.4, R9-BtnModoSoloUnMotor.Pin_1
  N14: LED_Error.anode, R11-Led_ErrorSD.Pin_0
  N15: Sensor_Voltaje.GND, Mod2.Connector_4, Mod1.-
  N16: Foto_Celda.pin1, Mod2.Connector_6
  N17: Foto_Celda.pin2, Mod2.Connector_5
  N18: Regulado_Voltaje_DC-DC_-12V_5V-5_7A.OUT+, Componente1.VIN
  N19: Bat_1.+#0, Bat_2.+#0, Mod1.12.6V
  N20: Bat_1.+#1, Bat_2.+#1, Bat_3.+#0, Mod1.8.4V, Bat4.+#0
  N21: Bat_3.+#1, Bat5.+#0, Bat6.+#0, Mod1.4.2V, Bat4.+#1
  N22: Bat5.+#1, Bat6.+#1, Mod1.0V

custom parts:
  Tiny RTC: Tiny RTC I2C module DS1370Z RTC and AT24C32 EEPROM
  ACS712 Current Sensor 5A 20A 30A: Remix by Michael Kubina http://www.kubina.info Original by: https://forum.fritzing.org/t/current-sensor-5a-acs712/7694 https://forum.fritzing.org/u/ArtHome ArtHome12@gmail.com
  Bluetooth HC-06u: Bluetooth HC-06 - face up, pins down 16.5mm x 37.5mm PCB
  Mini-360 DC-DC Buck converter: Mini-360 DC-DC Buck converter. Tiny buck step down voltage converter, input voltage 4.75 to 23V output 1 to 17V adjustable. Available from ebay and the like.
  Solar Charge Controller: PWM-Solar Charge Controller
  NodeMCU V3.0: ESP8266 based NodeMCU
  battery_holder_single_18650: single 18650 battery holder
  3S-BMS: 3S-BMS LIPO battery charger / protection unit. Note pcb does not match the board as it will likely connect with wires, so pcb is 6 pads suitable for .1in header pins.
