# Fritzing sketch Diagrama Solar Tracker (saved by Fritzing 1.0.0rc)
circuit board: 16.9333cm x 5.64444cm
breadboards: 1

parts:
  LED_ModoManual = LED - 5mm [color="Blue (505nm)" current=0.030A package="5 mm [THT]"]
  LED_SoloMotorHorizontal = LED - 5mm [color="Blue (505nm)" current=0.030A package="5 mm [THT]"]
  LED_ModoAutomatico = LED - 5mm [color="Blue (525nm)" current=0.030A part_number=Led_BTN_Automatico package="5 mm [THT]"]
  R6-LEDModoAutomatico = Resistor [tolerance=±5% resistance=220 power=0.25W package=THT]
  R2-Right_-_10k = Resistor [tolerance=±5% resistance=10k power=0.25W package=THT]
  R3_-_Down_10k = Resistor [tolerance=±5% resistance=10k power=0.25W package=THT]
  R4_-UP_10k = Resistor [tolerance=±5% resistance=10k power=0.25W package=THT]
  R1-_Left_10k = Resistor [tolerance=±5% resistance=10k power=0.25W package=THT]
  Servo_Vertical = Basic Servo [part_number="HiTec HS-422"]
  LDR_2_Right = Photocell (LDR) [power=0.25W dark_resistance_@0.01lx=300kΩ light_resistance_@100lx=400Ω luminance=10lx package=THT]
  LDR_3_UP_PIN_A3 = Photocell (LDR) [power=0.25W dark_resistance_@0.01lx=300kΩ light_resistance_@100lx=400Ω luminance=10lx package=THT]
  LDR_4_Down_PIN_A2 = Photocell (LDR) [power=0.25W dark_resistance_@0.01lx=300kΩ light_resistance_@100lx=400Ω luminance=10lx package=THT]
  Reloj_Tinyu_RTC = Tiny RTC
  Sensor_Amperaje_ACS712 = ACS712 Current Sensor 5A 20A 30A
  Pla_Cprincipal = Arduino Mega 2560 (Rev3)
  Servo_Horizonal = Basic Servo [part_number="HiTec HS-422"]
  Pantalla_OLED_I2C1 = OLED 128x64 I2C Monochrome Display
  Foto_Celda = Solar Pannel [part_number=FotoSelda]
  R12-MedirNivelBateria = Resistor [tolerance=±5% resistance=10k power=0.25W package=THT]
  Bluetooth = Bluetooth HC-06u [package=THT]
  Joystick_KY_023 = Thumb Joystick
  BTN_ModoManual = Momentary Switch [package=ksa_sealed_tac_switch]
  Switch-_Encendido = Round Pushbutton
  BTN_ModoAutomatico = Momentary Switch [package=ksa_sealed_tac_switch]
  BTN_SoloMotorHorizontal = Momentary Switch [package=ksa_sealed_tac_switch]
  R8-BtnModoManual = Resistor [tolerance=±5% power=0.25W resistance=10 package=THT]
  R9-BtnModoSoloUnMotor = Resistor [tolerance=±5% power=0.25W resistance=10 package=THT]
  R10-ModoAutomatico = Resistor [tolerance=±5% power=0.25W resistance=10 package=THT]
  R6-LEDModoSoloUnMotor = Resistor [tolerance=±5% power=0.25W resistance=220 package=THT]
  R5-LED_ModoManual = Resistor [tolerance=±5% power=0.25W resistance=220 package=THT]
  R18 = Resistor [tolerance=±5% power=0.25W resistance=220 package=THT]
  LED_Encendido = LED - 5mm [color="Red (633nm)" current=0.030A package="5 mm [THT]"]
  LED_ErrorSD = LED - 5mm [color="Red (633nm)" current=0.030A package="5 mm [THT]"]
  Sensor_Voltaje = Voltage Sensor 25V
  LDR_1_Left = Photocell (LDR) [power=0.25W dark_resistance_@0.01lx=300kΩ light_resistance_@100lx=400Ω luminance=10lx package=THT]
  Modulo_de_carga_HX-4S-A01 = 3s-bms_1
  Bat1 = 1x_18650_battery_holder
  Bat2 = 1x_18650_battery_holder
  Bat3 = 1x_18650_battery_holder
  Bat4 = 1x_18650_battery_holder
  R11-Led_ErrorSD = Resistor [tolerance=±5% power=0.25W resistance=220 package=THT]

nets (from the schematic view):
  N1: LED_ModoManual.anode, R5-LED_ModoManual.Pin_1
  N2: LED_SoloMotorHorizontal.cathode, LED_ModoAutomatico.cathode, LED_Encendido.cathode
  N3: LED_SoloMotorHorizontal.anode, R6-LEDModoSoloUnMotor.Pin_1
  N4: LED_ModoAutomatico.anode, R6-LEDModoAutomatico.Pin_1
  VCC: R6-LEDModoAutomatico.Pin_0, Servo_Vertical.vcc, Reloj_Tinyu_RTC.VCC, Sensor_Amperaje_ACS712.VCC, Pla_Cprincipal.5V, Servo_Horizonal.vcc, Pantalla_OLED_I2C1.VDD, Bluetooth.VCC, Joystick_KY_023.VCC, BTN_ModoManual.1, BTN_ModoAutomatico.1, BTN_SoloMotorHorizontal.1, R6-LEDModoSoloUnMotor.Pin_0, R5-LED_ModoManual.Pin_0, R18.Pin_1
  N5: R2-Right_-_10k.Pin_0, LDR_2_Right.pin_1
  GND: R2-Right_-_10k.Pin_1, R3_-_Down_10k.Pin_0, R4_-UP_10k.Pin_0, R1-_Left_10k.Pin_1, Servo_Vertical.gnd, Reloj_Tinyu_RTC.GND#10, Pla_Cprincipal.GND, Servo_Horizonal.gnd, Pantalla_OLED_I2C1.GND, Bluetooth.GND, Joystick_KY_023.GND, R8-BtnModoManual.Pin_0, R9-BtnModoSoloUnMotor.Pin_0, R10-ModoAutomatico.Pin_0
  N6: R3_-_Down_10k.Pin_1, LDR_4_Down_PIN_A2.pin_1
  N7: R4_-UP_10k.Pin_1, LDR_3_UP_PIN_A3.pin_1
  N8: R1-_Left_10k.Pin_0, LDR_1_Left.pin_1
  N9: Servo_Vertical.pulse, Pla_Cprincipal.D6_PWM
  N10: LDR_2_Right.pin_0, Pla_Cprincipal.A1
  N11: LDR_3_UP_PIN_A3.pin_0, Pla_Cprincipal.A2
  N12: LDR_4_Down_PIN_A2.pin_0, Pla_Cprincipal.A3
  N13: Reloj_Tinyu_RTC.GND#4, LED_ErrorSD.cathode
  N14: Reloj_Tinyu_RTC.SCL, Pla_Cprincipal.D21/SCL, Pla_Cprincipal.SCL, Pantalla_OLED_I2C1.SCK
  N15: Reloj_Tinyu_RTC.SDA, Pla_Cprincipal.D20/SDA, Pantalla_OLED_I2C1.SDA
  N16: Sensor_Amperaje_ACS712.1, Modulo_de_carga_HX-4S-A01.connector4
  3V3: Sensor_Amperaje_ACS712.2, Sensor_Amperaje_ACS712.OUT, Pla_Cprincipal.A4, Pla_Cprincipal.3V3, Foto_Celda.pin2, Sensor_Voltaje.VCC, Sensor_Voltaje.+
  GND_2: Sensor_Amperaje_ACS712.GND, Foto_Celda.pin1, BTN_ModoAutomatico.4, R10-ModoAutomatico.Pin_1, Sensor_Voltaje.GND, Sensor_Voltaje.-, Modulo_de_carga_HX-4S-A01.connector3
  N17: Pla_Cprincipal.A8, Sensor_Voltaje.S
  N18: Pla_Cprincipal.A0, LDR_1_Left.pin_0
  N19: Pla_Cprincipal.A5, R12-MedirNivelBateria.Pin_1
  N20: Pla_Cprincipal.A6, Joystick_KY_023.HORZ
  N21: Pla_Cprincipal.A7, Joystick_KY_023.VERT
  N22: Pla_Cprincipal.D17_PWM/RX2, Bluetooth.TXD
  N23: Pla_Cprincipal.D16_PWM/TX2, Bluetooth.RXD
  N24: Pla_Cprincipal.D13_PWM, R11-Led_ErrorSD.Pin_1
  N25: Pla_Cprincipal.VIN, Switch-_Encendido.leg1
  N26: Pla_Cprincipal.D7_PWM, Servo_Horizonal.pulse
  N27: BTN_ModoManual.4, R8-BtnModoManual.Pin_1
  N28: BTN_SoloMotorHorizontal.4, R9-BtnModoSoloUnMotor.Pin_1
  N29: R18.Pin_0, LED_Encendido.anode
  N30: LED_ErrorSD.anode, R11-Led_ErrorSD.Pin_0
  N31: Bat1.connector1, Bat2.connector0
  N32: Bat2.connector1, Bat3.connector0
  N33: Bat3.connector1, Bat4.connector0

custom parts:
  Tiny RTC: Tiny RTC I2C module DS1370Z RTC and AT24C32 EEPROM
  ACS712 Current Sensor 5A 20A 30A: Remix by Michael Kubina http://www.kubina.info Original by: https://forum.fritzing.org/t/current-sensor-5a-acs712/7694 https://forum.fritzing.org/u/ArtHome ArtHome12@gmail.com
  Bluetooth HC-06u: Bluetooth HC-06 - face up, pins down 16.5mm x 37.5mm PCB
